// Logisim project v2.circ as structural Verilog: 2 circuits, main circuit main
module main (
  input  A2,
  input  A3,
  input  A13,
  input  A14,
  input  A15,
  input  VMA,
  output nRAM1,
  output RAM2,
  output nROMce,
  output nROMoe,
  output PIAcs1,
  output nPIAcs2,
  output PIAcs0,
  output UARTcs0,
  output nUARTcs2,
  output UARTcs1
);

  wire and_1_out, and_2_out, and_3_out, and_4_out;

  not not_1 (nROMoe, A15);
  nand nand_1 (nROMce, A14, A13);
  and and_1 (and_1_out, ~A15, VMA);  // AND_Gate
  and and_2 (and_2_out, ~nROMce, ~nROMoe);  // AND_Gate
  and and_3 (and_3_out, A15, ~A2, VMA);  // AND_Gate
  and and_4 (and_4_out, A15, ~A3, A2);  // AND_Gate

  assign nPIAcs2 = A2;
  assign nRAM1 = A15;
  assign nUARTcs2 = A3;
  assign PIAcs0 = VMA;
  assign PIAcs1 = A15;
  assign RAM2 = VMA;
  assign UARTcs0 = A15;
  assign UARTcs1 = A2;
endmodule

module memory (
  input  A2,
  input  A3,
  input  A13,
  input  A14,
  input  A15,
  input  VMA,
  output nRAM1,
  output RAM2,
  output nROMce,
  output nROMoe,
  output PIAcs1,
  output nPIAcs2,
  output PIAcs0,
  output UARTcs0,
  output nUARTcs2,
  output UARTcs1
);

  not not_1 (nROMoe, A15);
  nand nand_1 (nROMce, A14, A13);

  assign nPIAcs2 = A2;
  assign nRAM1 = A15;
  assign nUARTcs2 = A3;
  assign PIAcs0 = VMA;
  assign PIAcs1 = A15;
  assign RAM2 = VMA;
  assign UARTcs0 = A15;
  assign UARTcs1 = A2;
endmodule
